# Fritzing sketch Projeto (saved by Fritzing 1.0.5)
breadboards: 1

parts:
  M1 = DOIT Esp32 DevKit v1 (30 pins long, 11 pins width) [part_number=ESP32S-PIN30]
  U1 = Battery Holders [package=lipo-1100mAh]
  L298N1 = L298N DC motor driver
  Componente1 = InvenSense MPU6050
  Componente2 = Adafruit VL530X Time of Flight Distance Sensor [part_number="Adafruit #3317"]
  M2 = DC Motor [voltage_(max)=6V voltage_(min)=3V]
  M3 = DC Motor [voltage_(max)=6V voltage_(min)=3V]
  M4 = DC Motor [voltage_(max)=6V voltage_(min)=3V]
  M5 = DC Motor [voltage_(max)=6V voltage_(min)=3V]

nets:
  VCC: M1.3V3, Componente1.VCC, Componente2.VCC
  N1: M1.D21, Componente1.SDA, Componente2.SDA
  N2: M1.D22, Componente1.SCL, Componente2.SCL
  VIN: M1.VIN, L298N1.5V
  N3: U1.+, L298N1.12V
  GND: U1.-, L298N1.GND, Componente1.GND, Componente2.GND
  N4: L298N1.OUT1, M4.pin_2, M5.pin_2
  N5: L298N1.OUT2, M4.pin_1, M5.pin_1
  N6: L298N1.OUT3, M2.pin_2, M3.pin_2
  N7: L298N1.OUT4, M2.pin_1, M3.pin_1

custom parts:
  DOIT Esp32 DevKit v1 (30 pins long, 11 pins width): The DOIT Esp32 DevKit v1 is one of the development board created by DOIT to evaluate the ESP-WROOM-32 module. It is based on the ESP32 microcontroller that boasts Wifi, Bluetooth, Ethernet and Low Power support all in a single chip. (vanepp) made breadboard work, adjusted pin numbering and labels and reduced size of schematic and cleaned up pcb. This chip is 30pins long (2 x15) and 11 pins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
  L298N DC motor driver: 2x DC motor driver with 78M05 positive voltage regulator (7..35 V) L298N: max 46 V, 2 A Set 5 V Enable jumper to enable 5 V regultor (needed for the L298N) and +5 V output at screw terminal or supply external +5 V at screw terminal Set ENA and/or ENB to +5 V to enable motor permanently or supply ENA and/or ENB with PWM signal IN1 and IN2 set rotation directory for motor A (OUT1/OUT2) IN2 and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
  Adafruit VL530X Time of Flight Distance Sensor: The VL53L0X is a Time of Flight distance sensor like no other you've used! The sensor contains a very tiny invisible laser source, and a matching sensor. The VL53L0X can detect the "time of flight", or how long the light has taken to bounce back to the sensor. Since it uses a very narrow light source, it is good for determining distance of only the surface directly in front of it. Unlike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
